// Logisim project SampleBoard_UsingLibs.circ as structural Verilog: 3 circuits, main circuit main
module main (
);

  wire addrdecoder_1_bootrom, addrdecoder_1_i_o, addrdecoder_1_mainram, addrdecoder_1_progrom, and_1_out,
       button_1_out, clock_1_out, keyboard_1_avail, perictl_1_p1_w, perictl_1_p2_r, stol_1_load,
       stol_1_store, stol_1_sysmode;
  wire [6:0] buffer_3_out, keyboard_1_data;
  wire [7:7] not_1_out;
  wire [15:0] bit_extender_1_out, BootROM_data, buffer_1_out, buffer_2_out, controlled_buffer_1_out,
       MainRAM_dout, perictl_1_d, ProgROM_data, stol_1_addr, stol_1_data;
  wire [15:7] buffer_3_out_2;

  Clock clock_1 (.out(clock_1_out));
  PeriCtl perictl_1 (
    .Addr(stol_1_addr), .R(stol_1_load), .W(stol_1_store), .CS(addrdecoder_1_i_o), .D(perictl_1_d),
    .P1_D({16{1'b0}}), .P1_W(perictl_1_p1_w), .P2_D(bit_extender_1_out), .P2_R(perictl_1_p2_r),
    .P3_D({16{1'b0}}), .in_8({16{1'b0}}));  // open: P1_R, P2_W, P3_R, P3_W, P4_R, P4_W
  STOL stol_1 (
    .MemIn(controlled_buffer_1_out), .Clk(clock_1_out), .IRQ(1'b0), .PRI(3'b000), .Reset(button_1_out),
    .SysMode(stol_1_sysmode), .Addr(stol_1_addr), .Data(stol_1_data), .Load(stol_1_load), .Store(stol_1_store));  // open: ACK, Execute
  Button button_1 (.out(button_1_out));
  TTY #(.rows(9)) tty_1 (.data(buffer_3_out), .clk(clock_1_out), .we(perictl_1_p1_w), .clr(1'b0));
  Keyboard keyboard_1 (
    .clk(clock_1_out), .re(perictl_1_p2_r), .clr(1'b0), .avail(keyboard_1_avail), .data(keyboard_1_data));
  AddrDecoder addrdecoder_1 (
    .A(stol_1_addr), .BootROM(addrdecoder_1_bootrom), .I_O(addrdecoder_1_i_o),
    .MainRAM(addrdecoder_1_mainram), .ProgRom(addrdecoder_1_progrom));
  assign buffer_1_out = stol_1_data;  // Buffer buffer_1, 16 bits wide
  assign buffer_2_out = buffer_1_out;  // Buffer buffer_2, 16 bits wide
  assign {buffer_3_out_2, buffer_3_out} = buffer_2_out;  // Buffer buffer_3, 16 bits wide
  and and_1 (and_1_out, stol_1_store, addrdecoder_1_mainram);
  not not_1 (not_1_out[7], keyboard_1_avail);
  ROM #(.dataWidth(16)) BootROM (.addr(stol_1_addr[7:0]), .data(BootROM_data));
  RAM #(.addrWidth(15), .dataWidth(16), .enables("line")) MainRAM (
    .addr(stol_1_addr[14:0]), .we(and_1_out), .clk(clock_1_out), .din({buffer_3_out_2, buffer_3_out}),
    .dout(MainRAM_dout));
  ROM #(.addrWidth(15), .dataWidth(16)) ProgROM (.addr(stol_1_addr[14:0]), .data(ProgROM_data));
  assign bit_extender_1_out = {{8{not_1_out[7]}}, {not_1_out[7], keyboard_1_data}};  // Bit_Extender bit_extender_1
  assign controlled_buffer_1_out = addrdecoder_1_bootrom ? BootROM_data : 16'bz;  // Controlled_Buffer controlled_buffer_1
  assign controlled_buffer_1_out = addrdecoder_1_mainram ? MainRAM_dout : 16'bz;  // Controlled_Buffer controlled_buffer_2
  assign controlled_buffer_1_out = addrdecoder_1_i_o ? perictl_1_d : 16'bz;  // Controlled_Buffer controlled_buffer_3
  assign controlled_buffer_1_out = addrdecoder_1_progrom ? ProgROM_data : 16'bz;  // Controlled_Buffer controlled_buffer_4

  // Notes on the sheet:
  //   contents of BootROM (hex, n*v repeats v):
  //   c4f0 7000 190f c4f0 8000 c400 100 c80c c710 1 9511 b0 fffd 110f d0f
  //   contents of ProgROM (hex, n*v repeats v):
  //   c400 100 c430 8010 c613 6431 9511 40 7 ca03 6431 4411 0 fffa 0 0 120 34*20 57 65 6c 63 6f 6d 65 20
  //   74 6f 20 74 68 65 20 53 54 4f 4c 20 63 6f 6d 70 75 74 65 72 36*20 43 68 65 63 6b 20 6f 75 74 20 74
  //   68 65 20 2e 2f 65 78 61 6d 70 6c 65 73 8*20 24 20 73 74 6f 6c 61 73 20 3c 66 69 6c 65 2e 73 20 3e 66
  //   69 6c 65 2e 6c 63 6f 64 65 6*20 72 69 67 68 74 20 63 6c 69 63 6b 20 50 72 6f 67 52 4f 4d 13*20 4c 6f
  //   61 64 20 49 6d 61 67 65 2e 2e 2e 19*20 73 65 6c 65 63 74 20 79 6f 75 72 20 66 69 6c 65 2e 6c 63 6f
  //   64 65 38*20
endmodule

module AddrDecoder (
  input  [15:0] A,
  output BootROM,
  output I_O,
  output MainRAM,
  output ProgRom
);

  wire and_1_out, buffer_1_out, buffer_2_out, buffer_3_out, buffer_4_out, buffer_5_out, buffer_6_out,
       buffer_7_out, buffer_8_out, nor_1_out, nor_2_out, or_1_out;

  nor nor_1 (nor_1_out, A[8], A[9], A[10], A[11], A[12], A[13], A[14], A[15]);
  nor nor_2 (nor_2_out, ~A[8], A[9], A[10], A[11], A[12], A[13], A[14], A[15]);  // NOR_Gate
  or or_1 (or_1_out, A[9], A[10], A[11], A[12], A[13], A[14]);
  buf buffer_1 (buffer_1_out, A[15]);
  buf buffer_2 (buffer_2_out, nor_1_out);
  buf buffer_3 (buffer_3_out, buffer_2_out);
  buf buffer_4 (buffer_4_out, nor_2_out);
  buf buffer_5 (buffer_5_out, buffer_4_out);
  and and_1 (and_1_out, or_1_out, ~buffer_1_out);  // AND_Gate
  buf buffer_6 (buffer_6_out, and_1_out);
  buf buffer_7 (buffer_7_out, buffer_1_out);
  buf buffer_8 (buffer_8_out, buffer_7_out);
  and and_2 (BootROM, buffer_2_out, buffer_3_out);
  and and_3 (I_O, buffer_4_out, buffer_5_out);
  and and_4 (MainRAM, and_1_out, buffer_6_out);
  and and_5 (ProgRom, buffer_7_out, buffer_8_out);

  // Notes on the sheet:
  //   Ensure break before make
endmodule

module PeriCtl (
  input  [15:0] P1_D,
  input  [15:0] Addr,
  input  R,
  input  [15:0] P2_D,
  input  W,
  input  [15:0] P3_D,
  input  CS,
  input  [15:0] in_8,
  output P1_R,
  output P1_W,
  output P2_R,
  output P2_W,
  output P3_R,
  output P3_W,
  output P4_R,
  output P4_W,
  output [15:0] D
);

  Demultiplexer #(.enable("true"), .select(2)) demultiplexer_1 (
    .out0(P1_R), .out1(P2_R), .out2(P3_R), .out3(P4_R), .in(R), .sel(Addr[1:0]), .en(CS));
  Demultiplexer #(.enable("true"), .select(2)) demultiplexer_2 (
    .out0(P1_W), .out1(P2_W), .out2(P3_W), .out3(P4_W), .in(W), .sel(Addr[1:0]), .en(CS));
  Multiplexer #(.select(2), .width(16)) multiplexer_1 (
    .in0(P1_D), .in1(P2_D), .in2(P3_D), .in3(in_8), .out(D), .sel(Addr[1:0]));
endmodule
