// Logisim project STOL.circ as structural Verilog: 1 circuit, main circuit STOL
module STOL (
  input  IRQ,
  input  [2:0] PRI,
  input  [15:0] MemIn,
  input  Clk,
  input  Reset,
  output ACK,
  output SysMode,
  output [15:0] Addr,
  output [15:0] Data,
  output Load,
  output Store,
  output Execute
);

  wire A_mem, A_WE, ACK_t, addr_REG, ALU_WE, and_3_out, B_mem, B_WE, data_SEL, imm_shift, IR_WE, or_1_out,
       pc_add, pc_load, pc_minusOne, pop, psp_OP, psp_WE, push, reg_mem, reg_WE, ROff_WE, status_WE, trap;
  wire [1:0] addr_SEL;
  wire [3:0] multiplexer_3_out, small_imm;
  wire [14:0] regwithdefault_1_q;
  wire [15:0] A_q, adder_1_out, alu_1_result, ALUout, ALUout_q, B_q, IR_q, multiplexer_1_out,
       multiplexer_2_out, multiplexer_4_out, multiplexer_5_out, multiplexer_6_out, multiplexer_7_out,
       multiplexer_8_out, multiplexer_9_out, multiplexer_10_out, multiplexer_11_out, progctr_1_q,
       regbank_1_rd, regbank_1_rs, regbank_1_sp, ROff_q, Status;
  wire [15:8] multiplexer_3_out_2;

  Register #(.width(1)) register_1 (.D(ACK_t), .en(1'b1), .clk(Clk), .Q(ACK), .clr(Reset));
  Multiplexer #(.width(16)) multiplexer_1 (.in0(ALUout), .in1({12'hf, small_imm}), .out(multiplexer_1_out), .sel(trap));
  Multiplexer #(.width(16)) multiplexer_2 (
    .in0(multiplexer_1_out), .in1({12'he, PRI, 1'b0}), .out(multiplexer_2_out), .sel(ACK));
  ProgCtr progctr_1 (
    .D(multiplexer_2_out), .Load(pc_load), .Add(pc_add), .MinusOne(pc_minusOne), .Clk(Clk), .Reset(Reset),
    .Q(progctr_1_q));
  RegWithDefault regwithdefault_1 (
    .D(Status), .WE(status_WE), .Clk(Clk), .RV(16'h8000), .Reset(Reset), .Q({SysMode, regwithdefault_1_q}));
  Register #(.width(16)) IR (.D(MemIn), .en(IR_WE), .clk(Clk), .Q(IR_q), .clr(1'b0));
  Multiplexer #(.width(16)) multiplexer_3 (
    .in0(IR_q), .in1(MemIn), .out({multiplexer_3_out_2, multiplexer_3_out, small_imm}), .sel(IR_WE));
  Multiplexer #(.width(16)) multiplexer_4 (.in0(ALUout), .in1(MemIn), .out(multiplexer_4_out), .sel(reg_mem));
  StateMachine statemachine_1 (
    .IRQ(IRQ), .PRI(PRI), .SR({SysMode, regwithdefault_1_q}),
    .I({multiplexer_3_out_2, multiplexer_3_out, small_imm}), .Clk(Clk), .Reset(Reset), .ACK(ACK_t),
    .pc_load(pc_load), .pc_add(pc_add), .pc_minusOne(pc_minusOne), .status_WE(status_WE), .IR_WE(IR_WE),
    .A_WE(A_WE), .A_mem(A_mem), .B_WE(B_WE), .B_mem(B_mem), .ROff_WE(ROff_WE), .ALU_WE(ALU_WE),
    .reg_WE(reg_WE), .reg_mem(reg_mem), .psp_OP(psp_OP), .psp_WE(psp_WE), .push(push), .pop(pop),
    .addr_SEL(addr_SEL), .addr_REG(addr_REG), .data_SEL(data_SEL), .mem_W(Store), .mem_R(Load),
    .execute(Execute));
  and and_1 (trap, multiplexer_3_out_2[15], multiplexer_3_out_2[14], ~multiplexer_3_out_2[13], multiplexer_3_out_2[12], ~multiplexer_3_out_2[11], multiplexer_3_out_2[10], ~multiplexer_3_out_2[9], multiplexer_3_out_2[8]);  // AND_Gate
  and and_2 (imm_shift, ~multiplexer_3_out_2[15], ~multiplexer_3_out_2[14], multiplexer_3_out_2[13], multiplexer_3_out_2[12], ~multiplexer_3_out_2[8]);  // AND_Gate
  RegBank regbank_1 (
    .S(SysMode), .D(multiplexer_4_out), .Dest(multiplexer_3_out), .Src(small_imm), .WE(reg_WE),
    .pspOP(psp_OP), .pspWE(psp_WE), .Push(push), .Pop(pop), .Clk(Clk), .Reset(Reset), .RD(regbank_1_rd),
    .RS(regbank_1_rs), .SP(regbank_1_sp));
  Multiplexer #(.width(16)) multiplexer_5 (
    .in0(regbank_1_rs), .in1({{12{1'b0}}, small_imm}), .out(multiplexer_5_out), .sel(or_1_out));
  or or_1 (or_1_out, imm_shift, and_3_out);
  and and_3 (and_3_out, data_SEL, ~Store);  // AND_Gate
  Register #(.width(16)) ROff (.D(MemIn), .en(ROff_WE), .clk(Clk), .Q(ROff_q), .clr(1'b0));
  Register #(.width(16)) A (.D(multiplexer_6_out), .en(A_WE), .clk(Clk), .Q(A_q), .clr(1'b0));
  Multiplexer #(.width(16)) multiplexer_6 (.in0(regbank_1_rd), .in1(MemIn), .out(multiplexer_6_out), .sel(A_mem));
  Register #(.width(16)) B (.D(multiplexer_7_out), .en(B_WE), .clk(Clk), .Q(B_q), .clr(1'b0));
  Multiplexer #(.width(16)) multiplexer_7 (.in0(multiplexer_5_out), .in1(MemIn), .out(multiplexer_7_out), .sel(B_mem));
  Multiplexer #(.width(16)) multiplexer_8 (
    .in0({multiplexer_3_out_2, multiplexer_3_out, small_imm}), .in1(16'hd00), .out(multiplexer_8_out),
    .sel(ACK_t));
  Multiplexer #(.width(16)) multiplexer_9 (.in0(A_q), .in1(multiplexer_6_out), .out(multiplexer_9_out), .sel(A_WE));
  Multiplexer #(.width(16)) multiplexer_10 (.in0(B_q), .in1(multiplexer_7_out), .out(multiplexer_10_out), .sel(B_WE));
  Multiplexer #(.width(16)) multiplexer_11 (
    .in0(regbank_1_rd), .in1(regbank_1_rs), .out(multiplexer_11_out), .sel(addr_REG));
  ALU alu_1 (
    .SR({SysMode, regwithdefault_1_q}), .A(multiplexer_9_out), .B(multiplexer_10_out),
    .Ins(multiplexer_8_out), .SR_out(Status), .Result(alu_1_result));
  Register #(.width(16)) u_ALUout (.D(alu_1_result), .en(ALU_WE), .clk(Clk), .Q(ALUout_q), .clr(1'b0));
  Adder #(.width(16)) adder_1 (.a(multiplexer_11_out), .b(ROff_q), .out(adder_1_out), .cin(1'b0));  // open: cout
  Multiplexer #(.width(16)) multiplexer_12 (.in0(ALUout_q), .in1(alu_1_result), .out(ALUout), .sel(ALU_WE));
  Multiplexer #(.width(16)) multiplexer_13 (.in0(ALUout), .in1(progctr_1_q), .out(Data), .sel(data_SEL));
  Multiplexer #(.select(2), .width(16)) multiplexer_14 (
    .in0(progctr_1_q), .in1(regbank_1_sp), .in2(multiplexer_11_out), .in3(adder_1_out), .out(Addr),
    .sel(addr_SEL));

  // Other names for the same wires on the sheet: exec = Execute; mem_R = Load; mem_W = Store;
  //   trap_addr[3:0] = small_imm; vec[3:1] = PRI
endmodule
