// Logisim project STOL_FSM.circ as structural Verilog: 10 circuits, main circuit State0
module State0 (
  input  uIRQ,
  input  C,
  input  [15:0] I,
  output [31:0] CW
);

  wire altstack, and_4_out, and_5_out, and_6_out, and_7_out, and_8_out, and_9_out, and_10_out, and_11_out,
       branch, call, condable, decoder_1_out1, decoder_1_out2, dest_imm, dmodes, or_5_out, push_pop, ret,
       smimm, smodes, src_imm, stackless, trap;
  wire [3:0] priority_encoder_1_out;
  wire [29:29] multiplexer_2_out;
  wire [31:0] multiplexer_1_out;

  or or_1 (smimm, I[0], I[1], I[2], I[3]);
  Decoder #(.enable("false"), .select(4)) decoder_1 (
    .out0(branch), .out1(decoder_1_out1), .out2(decoder_1_out2), .out13(trap), .sel(I[15:12]));  // open: out3, out4, out5, out6, out7, out8, out9, out10, out11, out12, out14, out15
  Decoder #(.select(2)) decoder_2 (.out2(call), .out3(ret), .sel(I[11:10]), .en(branch));  // open: out0, out1
  not not_1 (stackless, I[11]);
  xnor xnor_1 (src_imm, I[8], I[9]);
  xnor xnor_2 (dest_imm, I[10], I[11]);
  and and_1 (altstack, I[11], decoder_1_out1);
  and and_2 (push_pop, ~I[11], decoder_1_out1);  // AND_Gate
  or or_2 (dmodes, I[14], I[15]);
  or or_3 (smodes, dmodes, branch, decoder_1_out2);
  or or_4 (condable, branch, trap);
  and and_3 (CW[29], smimm, src_imm, ~I[9]);  // AND_Gate
  Multiplexer #(.width(32)) multiplexer_1 (
    .in0(32'h800d6600), .in1(32'h800d6200), .out(multiplexer_1_out), .sel(I[10]));
  and and_4 (and_4_out, push_pop, I[10]);
  and and_5 (and_5_out, push_pop, ~I[10]);  // AND_Gate
  or or_5 (or_5_out, call, trap);
  and and_6 (and_6_out, branch, stackless);
  and and_7 (and_7_out, condable, ~C);  // AND_Gate
  and and_8 (and_8_out, dmodes, I[11]);
  and and_9 (and_9_out, dmodes, dest_imm);
  and and_10 (and_10_out, smodes, I[9]);
  and and_11 (and_11_out, smodes, src_imm, ~CW[29]);  // AND_Gate
  Multiplexer #(.select(4), .width(32)) multiplexer_2 (
    .in0(32'h801d7400), .in4({8'h80, I[8], 2'b10, I[9], 20'hd7400}), .in5(32'h800d6408), .in6(32'h800d6407),
    .in7(32'h800d6406), .in8(32'h800d7405), .in9(multiplexer_1_out), .in10(32'h800d6400),
    .in11(32'h800d6404), .in12(32'h800d6403), .in13(32'h800d6402), .in14(32'h800d6401), .in15(32'h800d7105),
    .out({CW[31:30], multiplexer_2_out[29], CW[28:0]}), .sel(priority_encoder_1_out));  // open: in1, in2, in3
  Priority_Encoder #(.select(4)) priority_encoder_1 (
    .in0(1'b1), .in1(1'b0), .in2(1'b0), .in3(1'b0), .in4(altstack), .in5(and_4_out), .in6(and_5_out),
    .in7(ret), .in8(or_5_out), .in9(and_6_out), .in10(and_7_out), .in11(and_8_out), .in12(and_9_out),
    .in13(and_10_out), .in14(and_11_out), .in15(uIRQ), .out(priority_encoder_1_out), .en_in(1'b1));  // open: gs, en_out

  // Other names for the same wires on the sheet: absolute = I[10]; pop = I[10]; dest_ind = I[11]; asr = I[9];
  //   src_ind = I[9]; asw = I[8]; smallimm = CW[29]; irq = uIRQ; pass = C
endmodule

module State1 (
  input  C,
  input  [15:0] I,
  output [31:0] CW
);

  wire and_1_out, and_2_out, and_3_out, and_4_out, and_5_out, branch, call, decoder_1_out2, dest_imm, dmodes,
       smodes, stackless;
  wire [2:0] priority_encoder_1_out;
  wire [31:0] multiplexer_1_out;

  Decoder #(.enable("false"), .select(4)) decoder_1 (
    .out0(branch), .out2(decoder_1_out2), .sel(I[15:12]));  // open: out1, out3, out4, out5, out6, out7, out8, out9, out10, out11, out12, out13, out14, out15
  Decoder #(.select(2)) decoder_2 (.out2(call), .sel(I[11:10]), .en(branch));  // open: out0, out1, out3
  or or_1 (dmodes, I[14], I[15]);
  not not_1 (stackless, I[11]);
  xnor xnor_1 (dest_imm, I[10], I[11]);
  or or_2 (smodes, dmodes, branch, decoder_1_out2);
  Multiplexer #(.width(32)) multiplexer_1 (
    .in0(32'h800f0e00), .in1(32'h800f0200), .out(multiplexer_1_out), .sel(I[10]));
  and and_1 (and_1_out, branch, stackless);
  and and_2 (and_2_out, branch, ~C);  // AND_Gate
  and and_3 (and_3_out, dmodes, I[11]);
  and and_4 (and_4_out, dmodes, dest_imm);
  and and_5 (and_5_out, smodes, I[9]);
  Multiplexer #(.select(3), .width(32)) multiplexer_2 (
    .in0(32'h801f1400), .in2(32'h800f1405), .in3(multiplexer_1_out), .in4(32'h800f0400), .in5(32'h800f0404),
    .in6(32'h800f0403), .in7(32'h800f0402), .out(CW), .sel(priority_encoder_1_out));  // open: in1
  Priority_Encoder priority_encoder_1 (
    .in0(1'b1), .in1(1'b0), .in2(call), .in3(and_1_out), .in4(and_2_out), .in5(and_3_out), .in6(and_4_out),
    .in7(and_5_out), .out(priority_encoder_1_out), .en_in(1'b1));  // open: gs, en_out

  // Other names for the same wires on the sheet: src_ind = I[9]; absolute = I[10]; dest_ind = I[11]; pass = C
endmodule

module State2 (
  input  C,
  input  [15:0] I,
  output [31:0] CW
);

  wire and_3_out, and_4_out, and_5_out, branch, dest_imm, dest_ind, dmodes, xnor_2_out;
  wire [2:0] priority_encoder_1_out;
  wire [26:26] multiplexer_2_out;
  wire [31:0] multiplexer_1_out;

  nor nor_1 (branch, I[15], I[14], I[13], I[12]);
  xnor xnor_1 (CW[26], I[8], I[9]);
  or or_1 (dmodes, I[14], I[15]);
  xnor xnor_2 (xnor_2_out, I[10], I[11]);
  and and_1 (dest_ind, I[11], dmodes);
  and and_2 (dest_imm, xnor_2_out, dmodes);
  Multiplexer #(.width(32)) multiplexer_1 (
    .in0(32'h980f0e00), .in1(32'h980f0200), .out(multiplexer_1_out), .sel(I[10]));
  and and_3 (and_3_out, branch, I[11]);
  and and_4 (and_4_out, branch, ~I[11]);  // AND_Gate
  and and_5 (and_5_out, branch, ~C);  // AND_Gate
  Multiplexer #(.select(3), .width(32)) multiplexer_2 (
    .in0(32'h981f1000), .in3(32'h980f1005), .in4(multiplexer_1_out), .in5(32'h980f0000), .in6(32'h980f0004),
    .in7(32'h980f0003), .out({CW[31:27], multiplexer_2_out[26], CW[25:0]}), .sel(priority_encoder_1_out));  // open: in1, in2
  Priority_Encoder priority_encoder_1 (
    .in0(1'b1), .in1(1'b0), .in2(1'b0), .in3(and_3_out), .in4(and_4_out), .in5(and_5_out), .in6(dest_ind),
    .in7(dest_imm), .out(priority_encoder_1_out), .en_in(1'b1));  // open: gs, en_out

  // Other names for the same wires on the sheet: call = I[11]; pass = C
endmodule

module State3 (
  input  C,
  input  [15:0] I,
  output [31:0] CW
);


  assign CW = 32'h800cc404;
endmodule

module State4 (
  input  C,
  input  [15:0] I,
  output [31:0] CW
);

  assign CW = 32'h8808c009 | {{5{1'b0}}, I[10], {26{1'b0}}};  // OR_Gate or_1, 32 bits wide
endmodule

module State5 (
  input  C,
  input  [15:0] I,
  output [31:0] CW
);


  assign CW = 32'h65000200;
endmodule

module State6 (
  input  C,
  input  [15:0] I,
  output [31:0] CW
);


  assign CW = 32'h860b1200;
endmodule

module State7 (
  input  C,
  input  [15:0] I,
  output [31:0] CW
);


  assign CW = 32'h45001000;
endmodule

module State8 (
  input  C,
  input  [15:0] I,
  output [31:0] CW
);


  assign CW = 32'h86301000;
endmodule

module State9 (
  input  C,
  input  [15:0] I,
  output [31:0] CW
);

  assign CW = 32'h48001000 | {{5{1'b0}}, I[10], {26{1'b0}}};  // OR_Gate or_1, 32 bits wide
endmodule
