// Logisim project STOL_Helpers.circ as structural Verilog: 21 circuits, main circuit StateMachine
module StateMachine (
  input  IRQ,
  input  [2:0] PRI,
  input  [15:0] SR,
  input  [15:0] I,
  input  Clk,
  input  Reset,
  output ACK,
  output pc_load,
  output pc_add,
  output pc_minusOne,
  output status_WE,
  output IR_WE,
  output A_WE,
  output A_mem,
  output B_WE,
  output B_mem,
  output ROff_WE,
  output ALU_WE,
  output reg_WE,
  output reg_mem,
  output psp_OP,
  output psp_WE,
  output push,
  output pop,
  output [1:0] addr_SEL,
  output addr_REG,
  output data_SEL,
  output mem_W,
  output mem_R,
  output execute
);

  wire and_1_out, and_2_out, and_3_out, conditions_1_q, nor_2_out, unmasked_irq;
  wire [3:0] State_q;
  wire [7:0] multiplexer_1_out;
  wire [31:0] state0_1_cw, state1_1_cw, state2_1_cw, state3_1_cw, state4_1_cw, state5_1_cw, state6_1_cw,
       state7_1_cw, state8_1_cw, state9_1_cw;

  Register #(.width(4)) State (.D(multiplexer_1_out[3:0]), .en(1'b1), .clk(Clk), .Q(State_q), .clr(Reset));
  Conditions conditions_1 (.C(SR[3:0]), .Test(I[7:4]), .Q(conditions_1_q));
  State0 state0_1 (.uIRQ(unmasked_irq), .C(conditions_1_q), .I(I), .CW(state0_1_cw));
  State1 state1_1 (.C(conditions_1_q), .I(I), .CW(state1_1_cw));
  State2 state2_1 (.C(conditions_1_q), .I(I), .CW(state2_1_cw));
  State3 state3_1 (.C(conditions_1_q), .I(I), .CW(state3_1_cw));
  State4 state4_1 (.C(conditions_1_q), .I(I), .CW(state4_1_cw));
  State5 state5_1 (.C(conditions_1_q), .I(I), .CW(state5_1_cw));
  State6 state6_1 (.C(conditions_1_q), .I(I), .CW(state6_1_cw));
  State7 state7_1 (.C(conditions_1_q), .I(I), .CW(state7_1_cw));
  State8 state8_1 (.C(conditions_1_q), .I(I), .CW(state8_1_cw));
  State9 state9_1 (.C(conditions_1_q), .I(I), .CW(state9_1_cw));
  nor nor_1 (execute, State_q[0], State_q[1], State_q[2], State_q[3]);
  and and_1 (and_1_out, SR[6], ~PRI[2]);  // AND_Gate
  and and_2 (and_2_out, SR[6], SR[5], ~PRI[1]);  // AND_Gate
  Multiplexer #(.select(4), .width(32)) multiplexer_1 (
    .in0(state0_1_cw), .in1(state1_1_cw), .in2(state2_1_cw), .in3(state3_1_cw), .in4(state4_1_cw),
    .in5(state5_1_cw), .in6(state6_1_cw), .in7(state7_1_cw), .in8(state8_1_cw), .in9(state9_1_cw),
    .in10({32{1'b0}}), .in11({32{1'b0}}), .in12({32{1'b0}}), .in13({32{1'b0}}), .in14({32{1'b0}}),
    .in15({32{1'b0}}),
    .out({mem_R, mem_W, data_SEL, addr_REG, addr_SEL, pop, push, psp_WE, psp_OP, reg_mem, reg_WE, ALU_WE, ROff_WE, B_mem, B_WE, A_mem, A_WE, IR_WE, status_WE, pc_minusOne, pc_add, pc_load, ACK, multiplexer_1_out}),
    .sel(State_q));
  and and_3 (and_3_out, SR[6], SR[5], SR[4], ~PRI[0]);  // AND_Gate
  nor nor_2 (nor_2_out, and_3_out, and_2_out, and_1_out);
  and and_4 (unmasked_irq, nor_2_out, IRQ);

  // Notes on the sheet:
  //   is otherwise useless
  //   data_SEL without mem_W
  //   so save a pin and use this combo
  //   for "small immediate" load into B
endmodule

module RegBank (
  input  S,
  input  [15:0] D,
  input  [3:0] Dest,
  input  [3:0] Src,
  input  WE,
  input  pspOP,
  input  pspWE,
  input  Push,
  input  Pop,
  input  Clk,
  input  Reset,
  output [15:0] RD,
  output [15:0] RS,
  output [15:0] SP
);

  wire w0, w1, w2, w3, w4, w5, w6, w7, w8, w9, w10, w11, w12, w13, w14, w15;
  wire [15:0] multiplexer_1_out, psp, r0, r1, r2, r3, r4, r5, r6, r7, r8, r9, r10, r11, r12, r13, r14;

  Multiplexer #(.width(16)) multiplexer_1 (.in0(D), .in1(psp), .out(multiplexer_1_out), .sel(pspOP));
  Demultiplexer #(.select(4)) demultiplexer_1 (
    .out0(w0), .out1(w1), .out2(w2), .out3(w3), .out4(w4), .out5(w5), .out6(w6), .out7(w7), .out8(w8),
    .out9(w9), .out10(w10), .out11(w11), .out12(w12), .out13(w13), .out14(w14), .out15(w15), .in(WE),
    .sel(Dest));
  Register #(.width(16)) u_r0 (.D(multiplexer_1_out), .en(w0), .clk(Clk), .Q(r0), .clr(Reset));
  Register #(.width(16)) u_r4 (.D(multiplexer_1_out), .en(w4), .clk(Clk), .Q(r4), .clr(Reset));
  Register #(.width(16)) u_r8 (.D(multiplexer_1_out), .en(w8), .clk(Clk), .Q(r8), .clr(Reset));
  Register #(.width(16)) u_r12 (.D(multiplexer_1_out), .en(w12), .clk(Clk), .Q(r12), .clr(Reset));
  Register #(.width(16)) u_r1 (.D(multiplexer_1_out), .en(w1), .clk(Clk), .Q(r1), .clr(Reset));
  Register #(.width(16)) u_r5 (.D(multiplexer_1_out), .en(w5), .clk(Clk), .Q(r5), .clr(Reset));
  Register #(.width(16)) u_r9 (.D(multiplexer_1_out), .en(w9), .clk(Clk), .Q(r9), .clr(Reset));
  Register #(.width(16)) u_r13 (.D(multiplexer_1_out), .en(w13), .clk(Clk), .Q(r13), .clr(Reset));
  Register #(.width(16)) u_r2 (.D(multiplexer_1_out), .en(w2), .clk(Clk), .Q(r2), .clr(Reset));
  Register #(.width(16)) u_r6 (.D(multiplexer_1_out), .en(w4), .clk(Clk), .Q(r6), .clr(Reset));
  Register #(.width(16)) u_r10 (.D(multiplexer_1_out), .en(w10), .clk(Clk), .Q(r10), .clr(Reset));
  Register #(.width(16)) u_r14 (.D(multiplexer_1_out), .en(w14), .clk(Clk), .Q(r14), .clr(Reset));
  Register #(.width(16)) u_r3 (.D(multiplexer_1_out), .en(w3), .clk(Clk), .Q(r3), .clr(Reset));
  Register #(.width(16)) u_r7 (.D(multiplexer_1_out), .en(w7), .clk(Clk), .Q(r7), .clr(Reset));
  Register #(.width(16)) u_r11 (.D(multiplexer_1_out), .en(w11), .clk(Clk), .Q(r11), .clr(Reset));
  SPPair sppair_1 (
    .S(S), .D(multiplexer_1_out), .Src(RS), .WAlt(pspWE), .WE(w15), .Push(Push), .Pop(Pop), .Clk(Clk),
    .Reset(Reset), .SP(SP), .PSP(psp));  // open: SSP
  Multiplexer #(.select(4), .width(16)) multiplexer_2 (
    .in0(r0), .in1(r1), .in2(r2), .in3(r3), .in4(r4), .in5(r5), .in6(r6), .in7(r7), .in8(r8), .in9(r9),
    .in10(r10), .in11(r11), .in12(r12), .in13(r13), .in14(r14), .in15(SP), .out(RD), .sel(Dest));
  Multiplexer #(.select(4), .width(16)) multiplexer_3 (
    .in0(r0), .in1(r1), .in2(r2), .in3(r3), .in4(r4), .in5(r5), .in6(r6), .in7(r7), .in8(r8), .in9(r9),
    .in10(r10), .in11(r11), .in12(r12), .in13(r13), .in14(r14), .in15(SP), .out(RS), .sel(Src));

  // Other names for the same wires on the sheet: DSel[3:0] = Dest; r15[15:0] = SP; SSel[3:0] = Src
endmodule

module Conditions (
  input  [3:0] C,
  input  [3:0] Test,
  output Q
);

  wire multiplexer_1_out, or_1_out, or_2_out, xor_1_out;

  or or_1 (or_1_out, C[3], C[0]);
  xor xor_1 (xor_1_out, C[2], C[1]);
  Multiplexer #(.select(3)) multiplexer_1 (
    .in0(1'b1), .in1(C[3]), .in2(C[2]), .in3(C[1]), .in4(C[0]), .in5(or_1_out), .in6(xor_1_out),
    .in7(or_2_out), .out(multiplexer_1_out), .sel(Test[2:0]));
  or or_2 (or_2_out, xor_1_out, C[0]);
  xor xor_2 (Q, multiplexer_1_out, Test[3]);
endmodule

module ALU (
  input  [15:0] SR,
  input  [15:0] A,
  input  [15:0] B,
  input  [15:0] Ins,
  output [15:0] SR_out,
  output [15:0] Result
);

  wire and_1_out;
  wire [15:0] addsub_1_result, addsub_1_sro, clogic_1_sro, logic_1_result, logic_1_sro, multiplexer_1_out,
       senter_1_q, shifts_1_q, shifts_1_sro, sleave_1_q;

  CLogic clogic_1 (.SR(SR), .B(B), .I(Ins), .SRO(clogic_1_sro));
  Shifts shifts_1 (.SR(SR), .A(A), .B(B), .I(Ins), .SRO(shifts_1_sro), .Q(shifts_1_q));
  AddSub addsub_1 (.SR(SR), .A(A), .B(B), .I(Ins), .SRO(addsub_1_sro), .Result(addsub_1_result));
  Logic logic_1 (.SR(SR), .A(A), .B(B), .I(Ins), .SRO(logic_1_sro), .Result(logic_1_result));
  SLeave sleave_1 (.SR(SR), .Q(sleave_1_q));
  SEnter senter_1 (.SR(SR), .Q(senter_1_q));
  and and_1 (and_1_out, ~Ins[15], ~Ins[14], ~Ins[13], ~Ins[12], Ins[11], Ins[10], ~Ins[9], Ins[8], Ins[3], Ins[2], Ins[1], Ins[0]);  // AND_Gate
  Multiplexer #(.width(16)) multiplexer_1 (.in0(SR), .in1(sleave_1_q), .out(multiplexer_1_out), .sel(and_1_out));
  Multiplexer #(.select(4), .width(16)) multiplexer_2 (
    .in0(multiplexer_1_out), .in1(SR), .in2(clogic_1_sro), .in3(shifts_1_sro), .in4(addsub_1_sro),
    .in5(addsub_1_sro), .in6(addsub_1_sro), .in7(addsub_1_sro), .in8(addsub_1_sro), .in9(logic_1_sro),
    .in10(logic_1_sro), .in11(logic_1_sro), .in12(SR), .in13(senter_1_q), .in14(SR), .in15(SR), .out(SR_out),
    .sel(Ins[15:12]));
  Multiplexer #(.select(4), .width(16)) multiplexer_3 (
    .in0(B), .in1(B), .in2(SR), .in3(shifts_1_q), .in4(addsub_1_result), .in5(addsub_1_result),
    .in6(addsub_1_result), .in7(addsub_1_result), .in8(A), .in9(logic_1_result), .in10(logic_1_result),
    .in11(logic_1_result), .in12(B), .in13(B), .in14(B), .in15(B), .out(Result), .sel(Ins[15:12]));
endmodule

module ProgCtr (
  input  [15:0] D,
  input  Load,
  input  Add,
  input  MinusOne,
  input  Clk,
  input  Reset,
  output [15:0] Q
);

  wire [15:0] adder_1_out, adder_2_out, adder_3_out, bit_extender_1_out, multiplexer_1_out;

  Adder #(.width(16)) adder_1 (.a(Q), .b({16{1'b0}}), .out(adder_1_out), .cin(1'b1));  // open: cout
  Adder #(.width(16)) adder_2 (.a(D), .b(Q), .out(adder_2_out), .cin(1'b0));  // open: cout
  assign bit_extender_1_out = {{15{MinusOne}}, MinusOne};  // Bit_Extender bit_extender_1
  Multiplexer #(.select(2), .width(16)) multiplexer_1 (
    .in0(Q), .in1(adder_1_out), .in2(D), .in3(adder_2_out), .out(multiplexer_1_out), .sel({Load, Add}));
  Adder #(.width(16)) adder_3 (
    .a(multiplexer_1_out), .b(bit_extender_1_out), .out(adder_3_out), .cin(1'b0));  // open: cout
  Register #(.width(16)) PC (.D(adder_3_out), .en(1'b1), .clk(Clk), .Q(Q), .clr(Reset));

  // Notes on the sheet:
  //   Load = D
  //   Add = PC+1
  //   Load+Add = PC+D
endmodule

module RegWithDefault (
  input  [15:0] RV,
  input  [15:0] D,
  input  WE,
  input  Clk,
  input  Reset,
  output [15:0] Q
);

  wire multiplexer_2_out, nand_1_out, not_1_out, or_1_out;
  wire [15:0] multiplexer_1_out;

  not not_1 (not_1_out, Reset);
  nand nand_1 (nand_1_out, not_1_out, Reset);
  Multiplexer #(.width(16)) multiplexer_1 (.in0(D), .in1(RV), .out(multiplexer_1_out), .sel(Reset));
  Multiplexer multiplexer_2 (.in0(Clk), .in1(nand_1_out), .out(multiplexer_2_out), .sel(Reset));
  Register #(.width(16)) register_1 (.D(multiplexer_1_out), .en(or_1_out), .clk(multiplexer_2_out), .Q(Q), .clr(1'b0));
  or or_1 (or_1_out, WE, Reset);
endmodule

module SEnter (
  input  [15:0] SR,
  output [15:0] Q
);

  Adder #(.width(4)) adder_1 (.a(SR[11:8]), .b(4'b0000), .out(Q[11:8]), .cin(1'b1));  // open: cout

  assign {Q[15:12], Q[7:0]} = {1'b1, SR[14:12], SR[7:0]};
endmodule

module SLeave (
  input  [15:0] SR,
  output [15:0] Q
);

  wire nand_1_out;
  wire [3:0] subtractor_1_out;

  Subtractor #(.width(4)) subtractor_1 (.a(SR[11:8]), .b(4'b0000), .out(subtractor_1_out), .bin(1'b1));  // open: bout
  nand nand_1 (nand_1_out, subtractor_1_out[3], subtractor_1_out[2], subtractor_1_out[1], subtractor_1_out[0]);
  Multiplexer #(.width(4)) multiplexer_1 (.in0(SR[11:8]), .in1(subtractor_1_out), .out(Q[11:8]), .sel(SR[15]));
  and and_1 (Q[15], nand_1_out, SR[15]);

  assign {Q[14:12], Q[7:0]} = {SR[14:12], SR[7:0]};
endmodule

module Shifts (
  input  [15:0] SR,
  input  [15:0] A,
  input  [15:0] B,
  input  [15:0] I,
  output [15:0] SRO,
  output [15:0] Q
);

  wire asl_1_c, asl_1_v, asr_1_c, lsr_1_c, negcv_1_c, negcv_1_v;
  wire [3:0] bit_extender_1_out;
  wire [4:0] mod17_1_out_2;
  wire [15:0] asl_1_r, asr_1_q, lsr_1_q, negcv_1_result, shifter_1_out, shifter_2_out;
  wire [16:0] shifter_3_out, shifter_4_out;

  Bit_Extender #(.in_width(16), .out_width(4), .\type ("zero")) bit_extender_1 (.in(B), .out(bit_extender_1_out));
  mod17 mod17_1 (.in_1(B), .out_2(mod17_1_out_2));
  NegCV negcv_1 (.B(B), .C(negcv_1_c), .V(negcv_1_v), .Result(negcv_1_result));
  ASL asl_1 (.A(A), .B(B), .R(asl_1_r), .C(asl_1_c), .V(asl_1_v));
  LSR lsr_1 (.A(A), .B(B), .Q(lsr_1_q), .C(lsr_1_c));
  ASR asr_1 (.A(A), .B(B), .Q(asr_1_q), .C(asr_1_c));
  Shifter #(.shift("rl"), .width(16)) shifter_1 (.in(A), .\dist (bit_extender_1_out), .out(shifter_1_out));
  Shifter #(.shift("rr"), .width(16)) shifter_2 (.in(A), .\dist (bit_extender_1_out), .out(shifter_2_out));
  Shifter #(.shift("rl"), .width(17)) shifter_3 (.in({SR[3], A}), .\dist (mod17_1_out_2), .out(shifter_3_out));
  Shifter #(.shift("rr"), .width(17)) shifter_4 (.in({SR[3], A}), .\dist (mod17_1_out_2), .out(shifter_4_out));
  Multiplexer #(.select(3)) multiplexer_1 (
    .in0(negcv_1_v), .in1(1'b0), .in2(asl_1_v), .in3(1'b0), .in4(1'b0), .in5(1'b0), .in6(1'b0), .in7(1'b0),
    .out(SRO[2]), .sel(I[11:9]));
  Multiplexer #(.select(3)) multiplexer_2 (
    .in0(negcv_1_c), .in1(lsr_1_c), .in2(asl_1_c), .in3(asr_1_c), .in4(1'b0), .in5(1'b0),
    .in6(shifter_3_out[16]), .in7(shifter_4_out[16]), .out(SRO[3]), .sel(I[11:9]));
  Multiplexer #(.select(3), .width(16)) multiplexer_3 (
    .in0(negcv_1_result), .in1(lsr_1_q), .in2(asl_1_r), .in3(asr_1_q), .in4(shifter_1_out),
    .in5(shifter_2_out), .in6(shifter_3_out[15:0]), .in7(shifter_4_out[15:0]), .out(Q), .sel(I[11:9]));
  ZeroTest zerotest_1 (.in_1(Q), .out_2(SRO[0]));

  assign {SRO[15:4], SRO[1]} = {SR[15:4], Q[15]};
endmodule

module AddSub (
  input  [15:0] SR,
  input  [15:0] A,
  input  [15:0] B,
  input  [15:0] I,
  output [15:0] SRO,
  output [15:0] Result
);

  wire adder_1_cout, multiplexer_1_out, not_1_out, xnor_1_out, xor_2_out, xor_3_out;
  wire [15:0] bit_extender_1_out, xor_1_out;

  not not_1 (not_1_out, I[13]);
  assign xor_1_out = B ^ bit_extender_1_out;  // XOR_Gate xor_1, 16 bits wide
  assign bit_extender_1_out = {{15{not_1_out}}, not_1_out};  // Bit_Extender bit_extender_1
  xor xor_2 (xor_2_out, not_1_out, SR[3]);
  Multiplexer multiplexer_1 (.in0(not_1_out), .in1(xor_2_out), .out(multiplexer_1_out), .sel(I[12]));
  xor xor_3 (xor_3_out, xor_1_out[15], Result[15]);
  xnor xnor_1 (xnor_1_out, A[15], xor_1_out[15]);
  Adder #(.width(16)) adder_1 (.a(A), .b(xor_1_out), .out(Result), .cin(multiplexer_1_out), .cout(adder_1_cout));
  xor xor_4 (SRO[3], adder_1_cout, not_1_out);
  and and_1 (SRO[2], xor_3_out, xnor_1_out);
  ZeroTest zerotest_1 (.in_1(Result), .out_2(SRO[0]));

  assign {SRO[15:4], SRO[1]} = {SR[15:4], Result[15]};
endmodule

module NegCV (
  input  [15:0] B,
  output C,
  output V,
  output [15:0] Result
);

  wire zerotest_2_out_2;
  wire [15:15] not_1_out;

  not not_1 (not_1_out[15], B[15]);
  ZeroTest zerotest_1 (.in_1({not_1_out[15], B[14:0]}), .out_2(V));
  not not_2 (C, zerotest_2_out_2);
  ZeroTest zerotest_2 (.in_1(B), .out_2(zerotest_2_out_2));
  Negator #(.width(16)) negator_1 (.in(B), .out(Result));
endmodule

module CLogic (
  input  [15:0] SR,
  input  [15:0] B,
  input  [15:0] I,
  output [15:0] SRO
);

  wire [15:0] and_1_out, or_1_out, xor_1_out;
  wire [15:4] multiplexer_1_out;

  assign or_1_out = SR | B;  // OR_Gate or_1, 16 bits wide
  assign and_1_out = SR & B;  // AND_Gate and_1, 16 bits wide
  assign xor_1_out = SR ^ B;  // XOR_Gate xor_1, 16 bits wide
  Multiplexer #(.select(2), .width(16)) multiplexer_1 (
    .in0(B), .in1(or_1_out), .in2(and_1_out), .in3(xor_1_out), .out({multiplexer_1_out, SRO[3:0]}),
    .sel(I[11:10]));
  Multiplexer #(.width(12)) multiplexer_2 (.in0(SR[15:4]), .in1(multiplexer_1_out), .out(SRO[15:4]), .sel(SR[15]));
endmodule

module Logic (
  input  [15:0] SR,
  input  [15:0] A,
  input  [15:0] B,
  input  [15:0] I,
  output [15:0] SRO,
  output [15:0] Result
);

  wire [15:0] and_1_out, or_1_out, xor_1_out;

  assign or_1_out = A | B;  // OR_Gate or_1, 16 bits wide
  assign and_1_out = A & B;  // AND_Gate and_1, 16 bits wide
  assign xor_1_out = A ^ B;  // XOR_Gate xor_1, 16 bits wide
  Multiplexer #(.select(2), .width(16)) multiplexer_1 (
    .in0({16{1'b0}}), .in1(or_1_out), .in2(and_1_out), .in3(xor_1_out), .out(Result), .sel(I[13:12]));
  ZeroTest zerotest_1 (.in_1(Result), .out_2(SRO[0]));

  assign SRO[15:1] = {SR[15:2], Result[15]};
endmodule

module mod17 (
  input  [15:0] in_1,
  output [4:0] out_2
);

  wire decoder_1_out0, decoder_1_out1, decoder_1_out2, decoder_1_out3, decoder_1_out4, decoder_1_out5,
       decoder_1_out6, decoder_1_out7, decoder_1_out8, decoder_1_out9, decoder_1_out10, decoder_1_out11,
       decoder_1_out12, decoder_1_out13, decoder_1_out14, decoder_1_out15, mod17unit_1_out_19,
       mod17unit_1_out_20, mod17unit_1_out_21, mod17unit_1_out_22, mod17unit_1_out_23, mod17unit_1_out_24,
       mod17unit_1_out_25, mod17unit_1_out_26, mod17unit_1_out_27, mod17unit_1_out_28, mod17unit_1_out_29,
       mod17unit_1_out_30, mod17unit_1_out_31, mod17unit_1_out_32, mod17unit_1_out_33, mod17unit_1_out_34,
       mod17unit_1_out_35, mod17unit_2_out_19, mod17unit_2_out_20, mod17unit_2_out_21, mod17unit_2_out_22,
       mod17unit_2_out_23, mod17unit_2_out_24, mod17unit_2_out_25, mod17unit_2_out_26, mod17unit_2_out_27,
       mod17unit_2_out_28, mod17unit_2_out_29, mod17unit_2_out_30, mod17unit_2_out_31, mod17unit_2_out_32,
       mod17unit_2_out_33, mod17unit_2_out_34, mod17unit_2_out_35, mod17unit_3_out_19, mod17unit_3_out_20,
       mod17unit_3_out_21, mod17unit_3_out_22, mod17unit_3_out_23, mod17unit_3_out_24, mod17unit_3_out_25,
       mod17unit_3_out_26, mod17unit_3_out_27, mod17unit_3_out_28, mod17unit_3_out_29, mod17unit_3_out_30,
       mod17unit_3_out_31, mod17unit_3_out_32, mod17unit_3_out_33, mod17unit_3_out_34, mod17unit_3_out_35,
       mod17unit_4_out_19, mod17unit_4_out_20, mod17unit_4_out_21, mod17unit_4_out_22, mod17unit_4_out_23,
       mod17unit_4_out_24, mod17unit_4_out_25, mod17unit_4_out_26, mod17unit_4_out_27, mod17unit_4_out_28,
       mod17unit_4_out_29, mod17unit_4_out_30, mod17unit_4_out_31, mod17unit_4_out_32, mod17unit_4_out_33,
       mod17unit_4_out_34, mod17unit_4_out_35, mod17unit_5_out_19, mod17unit_5_out_20, mod17unit_5_out_21,
       mod17unit_5_out_22, mod17unit_5_out_23, mod17unit_5_out_24, mod17unit_5_out_25, mod17unit_5_out_26,
       mod17unit_5_out_27, mod17unit_5_out_28, mod17unit_5_out_29, mod17unit_5_out_30, mod17unit_5_out_31,
       mod17unit_5_out_32, mod17unit_5_out_33, mod17unit_5_out_34, mod17unit_5_out_35, mod17unit_6_out_19,
       mod17unit_6_out_20, mod17unit_6_out_21, mod17unit_6_out_22, mod17unit_6_out_23, mod17unit_6_out_24,
       mod17unit_6_out_25, mod17unit_6_out_26, mod17unit_6_out_27, mod17unit_6_out_28, mod17unit_6_out_29,
       mod17unit_6_out_30, mod17unit_6_out_31, mod17unit_6_out_32, mod17unit_6_out_33, mod17unit_6_out_34,
       mod17unit_6_out_35, mod17unit_7_out_19, mod17unit_7_out_20, mod17unit_7_out_21, mod17unit_7_out_22,
       mod17unit_7_out_23, mod17unit_7_out_24, mod17unit_7_out_25, mod17unit_7_out_26, mod17unit_7_out_27,
       mod17unit_7_out_28, mod17unit_7_out_29, mod17unit_7_out_30, mod17unit_7_out_31, mod17unit_7_out_32,
       mod17unit_7_out_33, mod17unit_7_out_34, mod17unit_7_out_35, mod17unit_8_out_19, mod17unit_8_out_20,
       mod17unit_8_out_21, mod17unit_8_out_22, mod17unit_8_out_23, mod17unit_8_out_24, mod17unit_8_out_25,
       mod17unit_8_out_26, mod17unit_8_out_27, mod17unit_8_out_28, mod17unit_8_out_29, mod17unit_8_out_30,
       mod17unit_8_out_31, mod17unit_8_out_32, mod17unit_8_out_33, mod17unit_8_out_34, mod17unit_8_out_35,
       mod17unit_9_out_19, mod17unit_9_out_20, mod17unit_9_out_21, mod17unit_9_out_22, mod17unit_9_out_23,
       mod17unit_9_out_24, mod17unit_9_out_25, mod17unit_9_out_26, mod17unit_9_out_27, mod17unit_9_out_28,
       mod17unit_9_out_29, mod17unit_9_out_30, mod17unit_9_out_31, mod17unit_9_out_32, mod17unit_9_out_33,
       mod17unit_9_out_34, mod17unit_9_out_35, mod17unit_10_out_19, mod17unit_10_out_20, mod17unit_10_out_21,
       mod17unit_10_out_22, mod17unit_10_out_23, mod17unit_10_out_24, mod17unit_10_out_25,
       mod17unit_10_out_26, mod17unit_10_out_27, mod17unit_10_out_28, mod17unit_10_out_29,
       mod17unit_10_out_30, mod17unit_10_out_31, mod17unit_10_out_32, mod17unit_10_out_33,
       mod17unit_10_out_34, mod17unit_10_out_35, mod17unit_11_out_19, mod17unit_11_out_20,
       mod17unit_11_out_21, mod17unit_11_out_22, mod17unit_11_out_23, mod17unit_11_out_24,
       mod17unit_11_out_25, mod17unit_11_out_26, mod17unit_11_out_27, mod17unit_11_out_28,
       mod17unit_11_out_29, mod17unit_11_out_30, mod17unit_11_out_31, mod17unit_11_out_32,
       mod17unit_11_out_33, mod17unit_11_out_34, mod17unit_11_out_35, mod17unit_12_out_19,
       mod17unit_12_out_20, mod17unit_12_out_21, mod17unit_12_out_22, mod17unit_12_out_23,
       mod17unit_12_out_24, mod17unit_12_out_25, mod17unit_12_out_26, mod17unit_12_out_27,
       mod17unit_12_out_28, mod17unit_12_out_29, mod17unit_12_out_30, mod17unit_12_out_31,
       mod17unit_12_out_32, mod17unit_12_out_33, mod17unit_12_out_34, mod17unit_12_out_35;

  Decoder #(.enable("false"), .select(4)) decoder_1 (
    .out0(decoder_1_out0), .out1(decoder_1_out1), .out2(decoder_1_out2), .out3(decoder_1_out3),
    .out4(decoder_1_out4), .out5(decoder_1_out5), .out6(decoder_1_out6), .out7(decoder_1_out7),
    .out8(decoder_1_out8), .out9(decoder_1_out9), .out10(decoder_1_out10), .out11(decoder_1_out11),
    .out12(decoder_1_out12), .out13(decoder_1_out13), .out14(decoder_1_out14), .out15(decoder_1_out15),
    .sel(in_1[15:12]));
  mod17unit mod17unit_1 (
    .in_1(decoder_1_out0), .in_2(decoder_1_out1), .in_3(decoder_1_out2), .in_4(decoder_1_out3),
    .in_5(decoder_1_out4), .in_6(decoder_1_out5), .in_7(decoder_1_out6), .in_8(decoder_1_out7),
    .in_9(decoder_1_out8), .in_10(decoder_1_out9), .in_11(decoder_1_out10), .in_12(decoder_1_out11),
    .in_13(decoder_1_out12), .in_14(decoder_1_out13), .in_15(decoder_1_out14), .in_16(decoder_1_out15),
    .in_17(1'b0), .in_18(in_1[11]), .out_19(mod17unit_1_out_19), .out_20(mod17unit_1_out_20),
    .out_21(mod17unit_1_out_21), .out_22(mod17unit_1_out_22), .out_23(mod17unit_1_out_23),
    .out_24(mod17unit_1_out_24), .out_25(mod17unit_1_out_25), .out_26(mod17unit_1_out_26),
    .out_27(mod17unit_1_out_27), .out_28(mod17unit_1_out_28), .out_29(mod17unit_1_out_29),
    .out_30(mod17unit_1_out_30), .out_31(mod17unit_1_out_31), .out_32(mod17unit_1_out_32),
    .out_33(mod17unit_1_out_33), .out_34(mod17unit_1_out_34), .out_35(mod17unit_1_out_35));
  mod17unit mod17unit_2 (
    .in_1(mod17unit_1_out_19), .in_2(mod17unit_1_out_20), .in_3(mod17unit_1_out_21),
    .in_4(mod17unit_1_out_22), .in_5(mod17unit_1_out_23), .in_6(mod17unit_1_out_24),
    .in_7(mod17unit_1_out_25), .in_8(mod17unit_1_out_26), .in_9(mod17unit_1_out_27),
    .in_10(mod17unit_1_out_28), .in_11(mod17unit_1_out_29), .in_12(mod17unit_1_out_30),
    .in_13(mod17unit_1_out_31), .in_14(mod17unit_1_out_32), .in_15(mod17unit_1_out_33),
    .in_16(mod17unit_1_out_34), .in_17(mod17unit_1_out_35), .in_18(in_1[10]), .out_19(mod17unit_2_out_19),
    .out_20(mod17unit_2_out_20), .out_21(mod17unit_2_out_21), .out_22(mod17unit_2_out_22),
    .out_23(mod17unit_2_out_23), .out_24(mod17unit_2_out_24), .out_25(mod17unit_2_out_25),
    .out_26(mod17unit_2_out_26), .out_27(mod17unit_2_out_27), .out_28(mod17unit_2_out_28),
    .out_29(mod17unit_2_out_29), .out_30(mod17unit_2_out_30), .out_31(mod17unit_2_out_31),
    .out_32(mod17unit_2_out_32), .out_33(mod17unit_2_out_33), .out_34(mod17unit_2_out_34),
    .out_35(mod17unit_2_out_35));
  mod17unit mod17unit_3 (
    .in_1(mod17unit_2_out_19), .in_2(mod17unit_2_out_20), .in_3(mod17unit_2_out_21),
    .in_4(mod17unit_2_out_22), .in_5(mod17unit_2_out_23), .in_6(mod17unit_2_out_24),
    .in_7(mod17unit_2_out_25), .in_8(mod17unit_2_out_26), .in_9(mod17unit_2_out_27),
    .in_10(mod17unit_2_out_28), .in_11(mod17unit_2_out_29), .in_12(mod17unit_2_out_30),
    .in_13(mod17unit_2_out_31), .in_14(mod17unit_2_out_32), .in_15(mod17unit_2_out_33),
    .in_16(mod17unit_2_out_34), .in_17(mod17unit_2_out_35), .in_18(in_1[9]), .out_19(mod17unit_3_out_19),
    .out_20(mod17unit_3_out_20), .out_21(mod17unit_3_out_21), .out_22(mod17unit_3_out_22),
    .out_23(mod17unit_3_out_23), .out_24(mod17unit_3_out_24), .out_25(mod17unit_3_out_25),
    .out_26(mod17unit_3_out_26), .out_27(mod17unit_3_out_27), .out_28(mod17unit_3_out_28),
    .out_29(mod17unit_3_out_29), .out_30(mod17unit_3_out_30), .out_31(mod17unit_3_out_31),
    .out_32(mod17unit_3_out_32), .out_33(mod17unit_3_out_33), .out_34(mod17unit_3_out_34),
    .out_35(mod17unit_3_out_35));
  mod17unit mod17unit_4 (
    .in_1(mod17unit_3_out_19), .in_2(mod17unit_3_out_20), .in_3(mod17unit_3_out_21),
    .in_4(mod17unit_3_out_22), .in_5(mod17unit_3_out_23), .in_6(mod17unit_3_out_24),
    .in_7(mod17unit_3_out_25), .in_8(mod17unit_3_out_26), .in_9(mod17unit_3_out_27),
    .in_10(mod17unit_3_out_28), .in_11(mod17unit_3_out_29), .in_12(mod17unit_3_out_30),
    .in_13(mod17unit_3_out_31), .in_14(mod17unit_3_out_32), .in_15(mod17unit_3_out_33),
    .in_16(mod17unit_3_out_34), .in_17(mod17unit_3_out_35), .in_18(in_1[8]), .out_19(mod17unit_4_out_19),
    .out_20(mod17unit_4_out_20), .out_21(mod17unit_4_out_21), .out_22(mod17unit_4_out_22),
    .out_23(mod17unit_4_out_23), .out_24(mod17unit_4_out_24), .out_25(mod17unit_4_out_25),
    .out_26(mod17unit_4_out_26), .out_27(mod17unit_4_out_27), .out_28(mod17unit_4_out_28),
    .out_29(mod17unit_4_out_29), .out_30(mod17unit_4_out_30), .out_31(mod17unit_4_out_31),
    .out_32(mod17unit_4_out_32), .out_33(mod17unit_4_out_33), .out_34(mod17unit_4_out_34),
    .out_35(mod17unit_4_out_35));
  mod17unit mod17unit_5 (
    .in_1(mod17unit_4_out_19), .in_2(mod17unit_4_out_20), .in_3(mod17unit_4_out_21),
    .in_4(mod17unit_4_out_22), .in_5(mod17unit_4_out_23), .in_6(mod17unit_4_out_24),
    .in_7(mod17unit_4_out_25), .in_8(mod17unit_4_out_26), .in_9(mod17unit_4_out_27),
    .in_10(mod17unit_4_out_28), .in_11(mod17unit_4_out_29), .in_12(mod17unit_4_out_30),
    .in_13(mod17unit_4_out_31), .in_14(mod17unit_4_out_32), .in_15(mod17unit_4_out_33),
    .in_16(mod17unit_4_out_34), .in_17(mod17unit_4_out_35), .in_18(in_1[7]), .out_19(mod17unit_5_out_19),
    .out_20(mod17unit_5_out_20), .out_21(mod17unit_5_out_21), .out_22(mod17unit_5_out_22),
    .out_23(mod17unit_5_out_23), .out_24(mod17unit_5_out_24), .out_25(mod17unit_5_out_25),
    .out_26(mod17unit_5_out_26), .out_27(mod17unit_5_out_27), .out_28(mod17unit_5_out_28),
    .out_29(mod17unit_5_out_29), .out_30(mod17unit_5_out_30), .out_31(mod17unit_5_out_31),
    .out_32(mod17unit_5_out_32), .out_33(mod17unit_5_out_33), .out_34(mod17unit_5_out_34),
    .out_35(mod17unit_5_out_35));
  mod17unit mod17unit_6 (
    .in_1(mod17unit_5_out_19), .in_2(mod17unit_5_out_20), .in_3(mod17unit_5_out_21),
    .in_4(mod17unit_5_out_22), .in_5(mod17unit_5_out_23), .in_6(mod17unit_5_out_24),
    .in_7(mod17unit_5_out_25), .in_8(mod17unit_5_out_26), .in_9(mod17unit_5_out_27),
    .in_10(mod17unit_5_out_28), .in_11(mod17unit_5_out_29), .in_12(mod17unit_5_out_30),
    .in_13(mod17unit_5_out_31), .in_14(mod17unit_5_out_32), .in_15(mod17unit_5_out_33),
    .in_16(mod17unit_5_out_34), .in_17(mod17unit_5_out_35), .in_18(in_1[6]), .out_19(mod17unit_6_out_19),
    .out_20(mod17unit_6_out_20), .out_21(mod17unit_6_out_21), .out_22(mod17unit_6_out_22),
    .out_23(mod17unit_6_out_23), .out_24(mod17unit_6_out_24), .out_25(mod17unit_6_out_25),
    .out_26(mod17unit_6_out_26), .out_27(mod17unit_6_out_27), .out_28(mod17unit_6_out_28),
    .out_29(mod17unit_6_out_29), .out_30(mod17unit_6_out_30), .out_31(mod17unit_6_out_31),
    .out_32(mod17unit_6_out_32), .out_33(mod17unit_6_out_33), .out_34(mod17unit_6_out_34),
    .out_35(mod17unit_6_out_35));
  mod17unit mod17unit_7 (
    .in_1(mod17unit_6_out_19), .in_2(mod17unit_6_out_20), .in_3(mod17unit_6_out_21),
    .in_4(mod17unit_6_out_22), .in_5(mod17unit_6_out_23), .in_6(mod17unit_6_out_24),
    .in_7(mod17unit_6_out_25), .in_8(mod17unit_6_out_26), .in_9(mod17unit_6_out_27),
    .in_10(mod17unit_6_out_28), .in_11(mod17unit_6_out_29), .in_12(mod17unit_6_out_30),
    .in_13(mod17unit_6_out_31), .in_14(mod17unit_6_out_32), .in_15(mod17unit_6_out_33),
    .in_16(mod17unit_6_out_34), .in_17(mod17unit_6_out_35), .in_18(in_1[5]), .out_19(mod17unit_7_out_19),
    .out_20(mod17unit_7_out_20), .out_21(mod17unit_7_out_21), .out_22(mod17unit_7_out_22),
    .out_23(mod17unit_7_out_23), .out_24(mod17unit_7_out_24), .out_25(mod17unit_7_out_25),
    .out_26(mod17unit_7_out_26), .out_27(mod17unit_7_out_27), .out_28(mod17unit_7_out_28),
    .out_29(mod17unit_7_out_29), .out_30(mod17unit_7_out_30), .out_31(mod17unit_7_out_31),
    .out_32(mod17unit_7_out_32), .out_33(mod17unit_7_out_33), .out_34(mod17unit_7_out_34),
    .out_35(mod17unit_7_out_35));
  mod17unit mod17unit_8 (
    .in_1(mod17unit_7_out_19), .in_2(mod17unit_7_out_20), .in_3(mod17unit_7_out_21),
    .in_4(mod17unit_7_out_22), .in_5(mod17unit_7_out_23), .in_6(mod17unit_7_out_24),
    .in_7(mod17unit_7_out_25), .in_8(mod17unit_7_out_26), .in_9(mod17unit_7_out_27),
    .in_10(mod17unit_7_out_28), .in_11(mod17unit_7_out_29), .in_12(mod17unit_7_out_30),
    .in_13(mod17unit_7_out_31), .in_14(mod17unit_7_out_32), .in_15(mod17unit_7_out_33),
    .in_16(mod17unit_7_out_34), .in_17(mod17unit_7_out_35), .in_18(in_1[4]), .out_19(mod17unit_8_out_19),
    .out_20(mod17unit_8_out_20), .out_21(mod17unit_8_out_21), .out_22(mod17unit_8_out_22),
    .out_23(mod17unit_8_out_23), .out_24(mod17unit_8_out_24), .out_25(mod17unit_8_out_25),
    .out_26(mod17unit_8_out_26), .out_27(mod17unit_8_out_27), .out_28(mod17unit_8_out_28),
    .out_29(mod17unit_8_out_29), .out_30(mod17unit_8_out_30), .out_31(mod17unit_8_out_31),
    .out_32(mod17unit_8_out_32), .out_33(mod17unit_8_out_33), .out_34(mod17unit_8_out_34),
    .out_35(mod17unit_8_out_35));
  mod17unit mod17unit_9 (
    .in_1(mod17unit_8_out_19), .in_2(mod17unit_8_out_20), .in_3(mod17unit_8_out_21),
    .in_4(mod17unit_8_out_22), .in_5(mod17unit_8_out_23), .in_6(mod17unit_8_out_24),
    .in_7(mod17unit_8_out_25), .in_8(mod17unit_8_out_26), .in_9(mod17unit_8_out_27),
    .in_10(mod17unit_8_out_28), .in_11(mod17unit_8_out_29), .in_12(mod17unit_8_out_30),
    .in_13(mod17unit_8_out_31), .in_14(mod17unit_8_out_32), .in_15(mod17unit_8_out_33),
    .in_16(mod17unit_8_out_34), .in_17(mod17unit_8_out_35), .in_18(in_1[3]), .out_19(mod17unit_9_out_19),
    .out_20(mod17unit_9_out_20), .out_21(mod17unit_9_out_21), .out_22(mod17unit_9_out_22),
    .out_23(mod17unit_9_out_23), .out_24(mod17unit_9_out_24), .out_25(mod17unit_9_out_25),
    .out_26(mod17unit_9_out_26), .out_27(mod17unit_9_out_27), .out_28(mod17unit_9_out_28),
    .out_29(mod17unit_9_out_29), .out_30(mod17unit_9_out_30), .out_31(mod17unit_9_out_31),
    .out_32(mod17unit_9_out_32), .out_33(mod17unit_9_out_33), .out_34(mod17unit_9_out_34),
    .out_35(mod17unit_9_out_35));
  mod17unit mod17unit_10 (
    .in_1(mod17unit_9_out_19), .in_2(mod17unit_9_out_20), .in_3(mod17unit_9_out_21),
    .in_4(mod17unit_9_out_22), .in_5(mod17unit_9_out_23), .in_6(mod17unit_9_out_24),
    .in_7(mod17unit_9_out_25), .in_8(mod17unit_9_out_26), .in_9(mod17unit_9_out_27),
    .in_10(mod17unit_9_out_28), .in_11(mod17unit_9_out_29), .in_12(mod17unit_9_out_30),
    .in_13(mod17unit_9_out_31), .in_14(mod17unit_9_out_32), .in_15(mod17unit_9_out_33),
    .in_16(mod17unit_9_out_34), .in_17(mod17unit_9_out_35), .in_18(in_1[2]), .out_19(mod17unit_10_out_19),
    .out_20(mod17unit_10_out_20), .out_21(mod17unit_10_out_21), .out_22(mod17unit_10_out_22),
    .out_23(mod17unit_10_out_23), .out_24(mod17unit_10_out_24), .out_25(mod17unit_10_out_25),
    .out_26(mod17unit_10_out_26), .out_27(mod17unit_10_out_27), .out_28(mod17unit_10_out_28),
    .out_29(mod17unit_10_out_29), .out_30(mod17unit_10_out_30), .out_31(mod17unit_10_out_31),
    .out_32(mod17unit_10_out_32), .out_33(mod17unit_10_out_33), .out_34(mod17unit_10_out_34),
    .out_35(mod17unit_10_out_35));
  mod17unit mod17unit_11 (
    .in_1(mod17unit_10_out_19), .in_2(mod17unit_10_out_20), .in_3(mod17unit_10_out_21),
    .in_4(mod17unit_10_out_22), .in_5(mod17unit_10_out_23), .in_6(mod17unit_10_out_24),
    .in_7(mod17unit_10_out_25), .in_8(mod17unit_10_out_26), .in_9(mod17unit_10_out_27),
    .in_10(mod17unit_10_out_28), .in_11(mod17unit_10_out_29), .in_12(mod17unit_10_out_30),
    .in_13(mod17unit_10_out_31), .in_14(mod17unit_10_out_32), .in_15(mod17unit_10_out_33),
    .in_16(mod17unit_10_out_34), .in_17(mod17unit_10_out_35), .in_18(in_1[1]), .out_19(mod17unit_11_out_19),
    .out_20(mod17unit_11_out_20), .out_21(mod17unit_11_out_21), .out_22(mod17unit_11_out_22),
    .out_23(mod17unit_11_out_23), .out_24(mod17unit_11_out_24), .out_25(mod17unit_11_out_25),
    .out_26(mod17unit_11_out_26), .out_27(mod17unit_11_out_27), .out_28(mod17unit_11_out_28),
    .out_29(mod17unit_11_out_29), .out_30(mod17unit_11_out_30), .out_31(mod17unit_11_out_31),
    .out_32(mod17unit_11_out_32), .out_33(mod17unit_11_out_33), .out_34(mod17unit_11_out_34),
    .out_35(mod17unit_11_out_35));
  mod17unit mod17unit_12 (
    .in_1(mod17unit_11_out_19), .in_2(mod17unit_11_out_20), .in_3(mod17unit_11_out_21),
    .in_4(mod17unit_11_out_22), .in_5(mod17unit_11_out_23), .in_6(mod17unit_11_out_24),
    .in_7(mod17unit_11_out_25), .in_8(mod17unit_11_out_26), .in_9(mod17unit_11_out_27),
    .in_10(mod17unit_11_out_28), .in_11(mod17unit_11_out_29), .in_12(mod17unit_11_out_30),
    .in_13(mod17unit_11_out_31), .in_14(mod17unit_11_out_32), .in_15(mod17unit_11_out_33),
    .in_16(mod17unit_11_out_34), .in_17(mod17unit_11_out_35), .in_18(in_1[0]), .out_19(mod17unit_12_out_19),
    .out_20(mod17unit_12_out_20), .out_21(mod17unit_12_out_21), .out_22(mod17unit_12_out_22),
    .out_23(mod17unit_12_out_23), .out_24(mod17unit_12_out_24), .out_25(mod17unit_12_out_25),
    .out_26(mod17unit_12_out_26), .out_27(mod17unit_12_out_27), .out_28(mod17unit_12_out_28),
    .out_29(mod17unit_12_out_29), .out_30(mod17unit_12_out_30), .out_31(mod17unit_12_out_31),
    .out_32(mod17unit_12_out_32), .out_33(mod17unit_12_out_33), .out_34(mod17unit_12_out_34),
    .out_35(mod17unit_12_out_35));
  Priority_Encoder #(.select(5)) priority_encoder_1 (
    .in0(mod17unit_12_out_19), .in1(mod17unit_12_out_20), .in2(mod17unit_12_out_21),
    .in3(mod17unit_12_out_22), .in4(mod17unit_12_out_23), .in5(mod17unit_12_out_24),
    .in6(mod17unit_12_out_25), .in7(mod17unit_12_out_26), .in8(mod17unit_12_out_27),
    .in9(mod17unit_12_out_28), .in10(mod17unit_12_out_29), .in11(mod17unit_12_out_30),
    .in12(mod17unit_12_out_31), .in13(mod17unit_12_out_32), .in14(mod17unit_12_out_33),
    .in15(mod17unit_12_out_34), .in16(mod17unit_12_out_35), .in17(1'b0), .in18(1'b0), .in19(1'b0),
    .in20(1'b0), .in21(1'b0), .in22(1'b0), .in23(1'b0), .in24(1'b0), .in25(1'b0), .in26(1'b0), .in27(1'b0),
    .in28(1'b0), .in29(1'b0), .in30(1'b0), .in31(1'b0), .out(out_2), .en_in(1'b1));  // open: gs, en_out
endmodule

module mod17unit (
  input  in_1,
  input  in_2,
  input  in_3,
  input  in_4,
  input  in_5,
  input  in_6,
  input  in_7,
  input  in_8,
  input  in_9,
  input  in_10,
  input  in_11,
  input  in_12,
  input  in_13,
  input  in_14,
  input  in_15,
  input  in_16,
  input  in_17,
  input  in_18,
  output out_19,
  output out_20,
  output out_21,
  output out_22,
  output out_23,
  output out_24,
  output out_25,
  output out_26,
  output out_27,
  output out_28,
  output out_29,
  output out_30,
  output out_31,
  output out_32,
  output out_33,
  output out_34,
  output out_35
);

  Multiplexer #(.width(17)) multiplexer_1 (
    .in0({in_9, in_17, in_8, in_16, in_7, in_15, in_6, in_14, in_5, in_13, in_4, in_12, in_3, in_11, in_2, in_10, in_1}),
    .in1({in_17, in_8, in_16, in_7, in_15, in_6, in_14, in_5, in_13, in_4, in_12, in_3, in_11, in_2, in_10, in_1, in_9}),
    .out({out_35, out_34, out_33, out_32, out_31, out_30, out_29, out_28, out_27, out_26, out_25, out_24, out_23, out_22, out_21, out_20, out_19}),
    .sel(in_18));
endmodule

module ZeroTest (
  input  [15:0] in_1,
  output out_2
);

  nor nor_1 (out_2, in_1[0], in_1[1], in_1[2], in_1[3], in_1[4], in_1[5], in_1[6], in_1[7], in_1[8], in_1[9], in_1[10], in_1[11], in_1[12], in_1[13], in_1[14], in_1[15], 1'b0);
endmodule

module ASL (
  input  [15:0] A,
  input  [15:0] B,
  output [15:0] R,
  output C,
  output V
);

  wire and_2_out, not_1_out, not_2_out, not_3_out, zerotest_1_out_2, zerotest_2_out_2, zerotest_3_out_2,
       zerotest_4_out_2;
  wire [4:0] bit_extender_1_out;
  wire [15:0] and_1_out, multiplexer_2_out, xor_16_out;
  wire [31:0] bit_extender_2_out, bit_extender_3_out, shifter_1_out, shifter_2_out;

  xor xor_1 (xor_16_out[15], multiplexer_2_out[15], R[15]);
  xor xor_2 (xor_16_out[14], multiplexer_2_out[14], R[15]);
  xor xor_3 (xor_16_out[13], multiplexer_2_out[13], R[15]);
  Bit_Extender #(.in_width(16), .out_width(5), .\type ("zero")) bit_extender_1 (.in(B), .out(bit_extender_1_out));
  xor xor_4 (xor_16_out[12], multiplexer_2_out[12], R[15]);
  xor xor_5 (xor_16_out[11], multiplexer_2_out[11], R[15]);
  xor xor_6 (xor_16_out[10], multiplexer_2_out[10], R[15]);
  assign bit_extender_2_out = {{16{1'b0}}, A};  // Bit_Extender bit_extender_2
  Shifter #(.width(32)) shifter_1 (.in(bit_extender_2_out), .\dist (bit_extender_1_out), .out(shifter_1_out));
  assign and_1_out = B & 16'hfff0;  // AND_Gate and_1, 16 bits wide
  assign bit_extender_3_out = {{16{A[15]}}, A};  // Bit_Extender bit_extender_3
  xor xor_7 (xor_16_out[9], multiplexer_2_out[9], R[15]);
  xor xor_8 (xor_16_out[8], multiplexer_2_out[8], R[15]);
  xor xor_9 (xor_16_out[7], multiplexer_2_out[7], R[15]);
  not not_1 (not_1_out, zerotest_1_out_2);
  ZeroTest zerotest_1 (.in_1(A), .out_2(zerotest_1_out_2));
  not not_2 (not_2_out, zerotest_2_out_2);
  ZeroTest zerotest_2 (.in_1(and_1_out), .out_2(zerotest_2_out_2));
  Shifter #(.width(32)) shifter_2 (.in(bit_extender_3_out), .\dist (bit_extender_1_out), .out(shifter_2_out));
  xor xor_10 (xor_16_out[6], multiplexer_2_out[6], R[15]);
  xor xor_11 (xor_16_out[5], multiplexer_2_out[5], R[15]);
  and and_2 (and_2_out, not_1_out, not_2_out);
  xor xor_12 (xor_16_out[4], multiplexer_2_out[4], R[15]);
  xor xor_13 (xor_16_out[3], multiplexer_2_out[3], R[15]);
  xor xor_14 (xor_16_out[2], multiplexer_2_out[2], R[15]);
  Multiplexer #(.width(16)) multiplexer_1 (.in0(shifter_1_out[15:0]), .in1({16{1'b0}}), .out(R), .sel(and_2_out));
  ZeroTest zerotest_3 (.in_1(shifter_1_out[31:16]), .out_2(zerotest_3_out_2));
  Multiplexer #(.width(16)) multiplexer_2 (
    .in0(shifter_2_out[31:16]), .in1(A), .out(multiplexer_2_out), .sel(and_2_out));
  xor xor_15 (xor_16_out[1], multiplexer_2_out[1], R[15]);
  xor xor_16 (xor_16_out[0], multiplexer_2_out[0], R[15]);
  not not_3 (not_3_out, zerotest_3_out_2);
  not not_4 (V, zerotest_4_out_2);
  ZeroTest zerotest_4 (.in_1(xor_16_out), .out_2(zerotest_4_out_2));
  or or_1 (C, not_3_out, and_2_out);
endmodule

module ASR (
  input  [15:0] A,
  input  [15:0] B,
  output [15:0] Q,
  output C
);

  wire and_2_out, not_1_out, not_2_out, not_3_out, zerotest_1_out_2, zerotest_2_out_2, zerotest_3_out_2;
  wire [4:0] bit_extender_1_out;
  wire [15:0] and_1_out, shifter_1_out;

  assign and_1_out = B & 16'hfff0;  // AND_Gate and_1, 16 bits wide
  not not_1 (not_1_out, zerotest_1_out_2);
  ZeroTest zerotest_1 (.in_1(A), .out_2(zerotest_1_out_2));
  Bit_Extender #(.in_width(16), .out_width(5)) bit_extender_1 (.in(B), .out(bit_extender_1_out));
  not not_2 (not_2_out, zerotest_2_out_2);
  ZeroTest zerotest_2 (.in_1(and_1_out), .out_2(zerotest_2_out_2));
  Shifter #(.shift("ar"), .width(32)) shifter_1 (
    .in({A, {16{1'b0}}}), .\dist (bit_extender_1_out), .out({Q, shifter_1_out}));
  ZeroTest zerotest_3 (.in_1(shifter_1_out), .out_2(zerotest_3_out_2));
  and and_2 (and_2_out, not_1_out, not_2_out);
  not not_3 (not_3_out, zerotest_3_out_2);
  or or_1 (C, not_3_out, and_2_out);
endmodule

module LSR (
  input  [15:0] A,
  input  [15:0] B,
  output [15:0] Q,
  output C
);

  wire and_2_out, not_1_out, not_2_out, not_3_out, zerotest_1_out_2, zerotest_2_out_2, zerotest_3_out_2;
  wire [4:0] bit_extender_1_out;
  wire [15:0] and_1_out, shifter_1_out;

  assign and_1_out = B & 16'hfff0;  // AND_Gate and_1, 16 bits wide
  not not_1 (not_1_out, zerotest_1_out_2);
  ZeroTest zerotest_1 (.in_1(A), .out_2(zerotest_1_out_2));
  Bit_Extender #(.in_width(16), .out_width(5)) bit_extender_1 (.in(B), .out(bit_extender_1_out));
  not not_2 (not_2_out, zerotest_2_out_2);
  ZeroTest zerotest_2 (.in_1(and_1_out), .out_2(zerotest_2_out_2));
  Shifter #(.shift("lr"), .width(32)) shifter_1 (
    .in({A, {16{1'b0}}}), .\dist (bit_extender_1_out), .out({Q, shifter_1_out}));
  ZeroTest zerotest_3 (.in_1(shifter_1_out), .out_2(zerotest_3_out_2));
  and and_2 (and_2_out, not_1_out, not_2_out);
  not not_3 (not_3_out, zerotest_3_out_2);
  or or_1 (C, not_3_out, and_2_out);
endmodule

module StackPointer (
  input  [15:0] D,
  input  WD,
  input  Predec,
  input  Postinc,
  input  Clk,
  input  Reset,
  output [15:0] Q
);

  wire [15:0] adder_1_out, multiplexer_1_out, multiplexer_2_out, sp_q, subtractor_1_out;

  Multiplexer #(.width(16)) multiplexer_1 (.in0(Q), .in1(D), .out(multiplexer_1_out), .sel(WD));
  Adder #(.width(16)) adder_1 (.a(multiplexer_1_out), .b({16{1'b0}}), .out(adder_1_out), .cin(1'b1));  // open: cout
  Multiplexer #(.width(16)) multiplexer_2 (
    .in0(multiplexer_1_out), .in1(adder_1_out), .out(multiplexer_2_out), .sel(Postinc));
  Register #(.width(16)) sp (.D(multiplexer_2_out), .en(1'b1), .clk(Clk), .Q(sp_q), .clr(Reset));
  Subtractor #(.width(16)) subtractor_1 (.a(sp_q), .b({16{1'b0}}), .out(subtractor_1_out), .bin(1'b1));  // open: bout
  Multiplexer #(.width(16)) multiplexer_3 (.in0(sp_q), .in1(subtractor_1_out), .out(Q), .sel(Predec));
endmodule

module SPPair (
  input  S,
  input  [15:0] D,
  input  [15:0] Src,
  input  WAlt,
  input  WE,
  input  Push,
  input  Pop,
  input  Clk,
  input  Reset,
  output [15:0] SP,
  output [15:0] PSP,
  output [15:0] SSP
);

  wire demultiplexer_1_out0, demultiplexer_1_out1, demultiplexer_2_out0, demultiplexer_2_out1,
       demultiplexer_3_out0, demultiplexer_3_out1, or_1_out;
  wire [15:0] multiplexer_1_out;

  Demultiplexer demultiplexer_1 (.out0(demultiplexer_1_out0), .out1(demultiplexer_1_out1), .in(WE), .sel(S));
  Demultiplexer demultiplexer_2 (.out0(demultiplexer_2_out0), .out1(demultiplexer_2_out1), .in(Push), .sel(S));
  Demultiplexer demultiplexer_3 (.out0(demultiplexer_3_out0), .out1(demultiplexer_3_out1), .in(Pop), .sel(S));
  Multiplexer #(.width(16)) multiplexer_1 (.in0(D), .in1(Src), .out(multiplexer_1_out), .sel(WAlt));
  or or_1 (or_1_out, WAlt, demultiplexer_1_out0);
  StackPointer stackpointer_1 (
    .D(multiplexer_1_out), .WD(or_1_out), .Predec(demultiplexer_2_out0), .Postinc(demultiplexer_3_out0),
    .Clk(Clk), .Reset(Reset), .Q(PSP));
  StackPointer stackpointer_2 (
    .D(D), .WD(demultiplexer_1_out1), .Predec(demultiplexer_2_out1), .Postinc(demultiplexer_3_out1),
    .Clk(Clk), .Reset(Reset), .Q(SSP));
  Multiplexer #(.width(16)) multiplexer_2 (.in0(PSP), .in1(SSP), .out(SP), .sel(S));
endmodule
